# Fritzing sketch controldoor (saved by Fritzing 0.8.7b)
breadboards: 1

parts:
  元件1 = Arduino Nano (Rev3.0) (ICSP)
  元件2 = Bluetooth Mate Silver
  DIP-Relay1 = DIP-Relay-D31A [part_number=D31A*]
  DIP-Relay2 = DIP-Relay-D31A [part_number=D31A*]
  7~12V = Power plug

nets:
  GND: 元件1.GND, 元件2.GND, DIP-Relay1.Coil2_-, DIP-Relay2.Coil2_-, 7~12V.GND
  N1: 元件1.D2, 元件2.TX_5V
  N2: 元件1.D4, 元件2.RX_5V
  N3: 元件1.D7, DIP-Relay2.COIL1_+
  N4: 元件1.D8, DIP-Relay1.COIL1_+
  VIN: 元件1.VIN, 7~12V.VCC
  3V3: 元件1.3V3, 元件2.VCC

notes:
  電動門遙控器(下)
  電動門遙控器(上)
